# Fritzing sketch wemos_d1_sensor (saved by Fritzing 0.9.3b)

parts:
  WeMos_D1_Mini1 = WeMos D1 Mini
  AM1 = AM2302 Humidity and Temperature Sensor

nets:
  3V3: WeMos_D1_Mini1.3V3, AM1.VDD
  N1: WeMos_D1_Mini1.D8, AM1.DATA
  N2: WeMos_D1_Mini1.G, AM1.GND
